# Fritzing sketch steckplatine (saved by Fritzing 0.9.3b)

parts:
  U1 = FS1000A - 433Mhz RF Transmitter [package=THT]
  U2 = XD-RF-5V [package=THT]
  Raspberry_Pi_1 = Raspberry Pi 3 [part_number=RPI-3-V1.2]

nets:
  N1: U1.DATA, Raspberry_Pi_1.GIPO17
  VCC: U1.VCC, Raspberry_Pi_1.5V
  GND: U1.GND, Raspberry_Pi_1.GND
  N2: U2.DATA, Raspberry_Pi_1.GIPO27

custom parts:
  FS1000A - 433Mhz RF Transmitter: This is 433Mhz RF transmitter with receiver kit for Arduino ARM MCU wireless Application environment: Remote control switch, receiver module, motorcycles, automobile anti-theft products, home security products, electric doors, shutter doors, windows, remote control socket, remote control LED, remote audio remote control electric doors, garage door remote control, remote control retractable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
  XD-RF-5V: This is 433Mhz RF transmitter with receiver kit for Arduino ARM MCU wireless Application environment: Remote control switch, receiver module, motorcycles, automobile anti-theft products, home security products, electric doors, shutter doors, windows, remote control socket, remote control LED, remote audio remote control electric doors, garage door remote control, remote control retractable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
